// Logisim project logismMilestone2.circ as structural Verilog
module mult8bit (
  input  [7:0] in_1,
  input  [7:0] in_2,
  output [13:0] out_3
);

  wire button_1_out, clock_1_out, nor_1_out, not_1_out, not_2_out, shift_register_2_p18,
       shift_register_2_p19, shift_register_2_p20, shift_register_2_p21, shift_register_2_p22,
       shift_register_2_p23, shift_register_2_p24, xor_1_out;
  wire [6:0] multiplexer_1_out, multiplexer_2_out, negator_1_out, negator_2_out;
  wire [13:0] adder_1_out, multiplexer_3_out, negator_3_out, register_1_q, shift_register_1_p13;

  Clock clock_1 (.out(clock_1_out));
  Negator #(.width(7)) negator_1 (.in(in_1[6:0]), .out(negator_1_out));
  Button button_1 (.out(button_1_out));
  Multiplexer #(.width(7)) multiplexer_1 (.in0(in_1[6:0]), .in1(negator_1_out), .out(multiplexer_1_out), .sel(in_1[7]));
  Negator #(.width(7)) negator_2 (.in(in_2[6:0]), .out(negator_2_out));
  not not_1 (not_1_out, button_1_out);
  Multiplexer #(.width(7)) multiplexer_2 (.in0(in_2[6:0]), .in1(negator_2_out), .out(multiplexer_2_out), .sel(in_2[7]));
  // Shift_Register #(.length(14)) shift_register_1: pin names not known; wires that end beside it: button_1_out, not_1_out, clock_1_out, 1'b0, multiplexer_1_out[0], multiplexer_1_out[1], multiplexer_1_out[2], multiplexer_1_out[3], multiplexer_1_out[4], multiplexer_1_out[5], multiplexer_1_out[6], 1'b0, shift_register_1_p13[0], shift_register_1_p13[1], shift_register_1_p13[2], shift_register_1_p13[3], shift_register_1_p13[4], shift_register_1_p13[5], shift_register_1_p13[6], shift_register_1_p13[7]
  // Shift_Register #(.length(7)) shift_register_2: pin names not known; wires that end beside it: button_1_out, not_1_out, clock_1_out, 1'b0, multiplexer_2_out[6], multiplexer_2_out[5], multiplexer_2_out[4], multiplexer_2_out[3], multiplexer_2_out[2], multiplexer_2_out[1], multiplexer_2_out[0], 1'b0, 1'b0, 1'b0, 1'b0, 1'b0, 1'b0, shift_register_2_p18, shift_register_2_p19, shift_register_2_p20, shift_register_2_p21, shift_register_2_p22, shift_register_2_p23, shift_register_2_p24, shift_register_1_p13[8], shift_register_1_p13[9], shift_register_1_p13[10], shift_register_1_p13[11], shift_register_1_p13[12], shift_register_1_p13[13]
  nor nor_1 (nor_1_out, shift_register_2_p18, shift_register_2_p19, shift_register_2_p20, shift_register_2_p21, shift_register_2_p22, shift_register_2_p23, shift_register_2_p24);
  Adder #(.width(14)) adder_1 (
    .a(register_1_q), .b(shift_register_1_p13), .out(adder_1_out), .cin(1'b0));  // open: cout
  Multiplexer #(.width(14)) multiplexer_3 (
    .in0({14{1'b0}}), .in1(adder_1_out), .out(multiplexer_3_out), .sel(shift_register_2_p24));
  not not_2 (not_2_out, nor_1_out);
  Register #(.width(14)) register_1 (
    .D(multiplexer_3_out), .en(not_2_out), .clk(clock_1_out), .Q(register_1_q), .clr(button_1_out));
  Multiplexer #(.width(14)) multiplexer_4 (.in0(register_1_q), .in1(negator_3_out), .out(out_3), .sel(xor_1_out));
  Negator #(.width(14)) negator_3 (.in(register_1_q), .out(negator_3_out));
  xor xor_1 (xor_1_out, in_2[7], in_1[7]);
endmodule

module ShiftLeft (
  input  in_1,
  output [6:0] out_2
);

  wire clock_1_out, d_ff_1_q, d_ff_2_q, d_ff_3_q, d_ff_4_q, d_ff_5_q, d_ff_6_q;

  Clock clock_1 (.out(clock_1_out));
  D_Flip_Flop d_ff_1 (.D(in_1), .clk(clock_1_out), .Q(d_ff_1_q));  // open: Qn, preset, reset
  D_Flip_Flop d_ff_2 (.D(d_ff_1_q), .clk(clock_1_out), .Q(d_ff_2_q));  // open: Qn, preset, reset
  D_Flip_Flop d_ff_3 (.D(d_ff_2_q), .clk(clock_1_out), .Q(d_ff_3_q));  // open: Qn, preset, reset
  D_Flip_Flop d_ff_4 (.D(d_ff_3_q), .clk(clock_1_out), .Q(d_ff_4_q));  // open: Qn, preset, reset
  D_Flip_Flop d_ff_5 (.D(d_ff_4_q), .clk(clock_1_out), .Q(d_ff_5_q));  // open: Qn, preset, reset
  D_Flip_Flop d_ff_6 (.D(d_ff_5_q), .clk(clock_1_out), .Q(d_ff_6_q));  // open: Qn, preset, reset
  D_Flip_Flop d_ff_7 (.D(d_ff_6_q), .clk(clock_1_out));  // open: Q, Qn, preset, reset
endmodule

module controlUnit (
  input  in_1,
  input  PSEL,
  input  in_3,
  output out_4
);


  assign out_4 = in_3;
  assign PSEL = in_1;
endmodule
